# Fritzing sketch GrowBro (saved by Fritzing 0.9.3b)
circuit board: 8.46667cm x 5.64444cm
breadboards: 1

parts:
  R1 = Trimmer Potentiometer [maximum_resistance=10kΩ package=THT]
  Q1 = NPN-Transistor [package="TO92 [THT]"]
  LCD1 = LCD screen
  RE1 = Rotary Encoder [package=THT]
  Part1 = Arduino Uno (Rev3)
  R3 = Resistor [tolerance=±5% resistance=1k package=THT]
  R4 = Resistor [tolerance=±5% resistance=1k package=THT]
  C1 = Ceramic Capacitor [capacitance=47nF package="100 mil [THT, multilayer]"]
  C2 = Ceramic Capacitor [capacitance=47nF package="100 mil [THT, multilayer]"]
  R5 = Resistor [tolerance=±5% resistance=1k package=THT]
  R6 = Resistor [tolerance=±5% resistance=1k package=THT]
  S1 = Pushbutton [package="[THT]"]
  C3 = Ceramic Capacitor [capacitance=47nF package="100 mil [THT, multilayer]"]
  R7 = Resistor [tolerance=±5% resistance=1k package=THT]
  U2 = RELAY [package=relay-jzc]
  D1 = Rectifier Diode [part_number=1N4001 package="300 mil [THT]"]
  Q2 = NPN-Transistor [package="TO92 [THT]"]
  R8 = Resistor [tolerance=±5% resistance=1k package=THT]
  R9 = Resistor [tolerance=±5% resistance=10k package=THT]
  R10 = Resistor [tolerance=±5% resistance=1k package=THT]

nets (from the breadboard view):
  VSS: R1.leg1, LCD1.VSS, LCD1.R/W, LCD1.LED-, RE1.EncoderPinA, Part1.GND, C1.1, C2.1, S1.Pin_1, S1.Pin_2, C3.1, U2.COIL1, D1.anode, R9.Pin_1
  N1: R1.wiper, LCD1.V0
  VDD: R1.leg2, LCD1.VDD, Part1.5V, R3.Pin_0, R8.Pin_0
  N2: Q1.E, LCD1.LED+
  N3: Q1.B, R4.Pin_1
  N4: Q1.C, R3.Pin_1
  N5: LCD1.RS, Part1.D12/MISO
  N6: LCD1.E, Part1.D11_PWM/MOSI
  N7: LCD1.DB4, Part1.D8
  N8: LCD1.DB5, Part1.D7
  N9: LCD1.DB6, Part1.D6_PWM
  N10: LCD1.DB7, Part1.D5_PWM
  N11: RE1.EncoderPinC, C2.0, R6.Pin_1
  N12: RE1.EncoderPinB, C1.0, R5.Pin_1
  N13: Part1.A0, R9.Pin_0
  N14: Part1.D9_PWM, U2.MAIN, D1.cathode
  N15: Part1.D10_PWM/SS, R4.Pin_0
  N16: Part1.D13/SCK, R10.Pin_0
  N17: Part1.D2, R5.Pin_0
  N18: Part1.D3_PWM, C3.0, R7.Pin_0
  N19: Part1.D4, R6.Pin_0
  N20: S1.Pin_3, S1.Pin_4, R7.Pin_1
  N21: Q2.B, R10.Pin_1
  N22: Q2.C, R8.Pin_1

notes:
  to pump
  to hum. sensor
